# Fritzing sketch dc-motor-measurement (saved by Fritzing 0.9.10b)

parts:
  V1 = AC Power [voltage=220V frequency=60]
  M3 = RioRand LM2596
  HLK-PM1 = HLK-PM12 [part_number=HLK-PM12]
  M2 = BTS7960
  M1 = DOIT Esp32 DevKit v1 (30 pins long, 11 pins width) [part_number=ESP32S-PIN30]
  M4 = DC Motor [voltage_(max)=12V voltage_(min)=5V]

nets:
  N1: V1.V+, HLK-PM1.AC_1
  N2: V1.V-, HLK-PM1.AC_2
  N3: M3.Pin_1, HLK-PM1.+Vo, M2.pin11
  N4: M3.Pin_2, HLK-PM1.-Vo, M2.pin12
  N5: M3.Pin_3, M2.pin7, M1.VIN
  N6: M3.Pin_4, M2.pin8, M1.GND
  N7: M2.pin1, M1.D13
  N8: M2.pin2, M1.D12
  N9: M2.pin3, M1.D14
  N10: M2.pin4, M1.D27
  N11: M2.pin9, M4.pin_1
  N12: M2.pin10, M4.pin_2

custom parts:
  BTS7960: BTS7960 43A Peak Power H-Bridge PWM Motor Driver
  DOIT Esp32 DevKit v1 (30 pins long, 11 pins width): The DOIT Esp32 DevKit v1 is one of the development board created by DOIT to evaluate the ESP-WROOM-32 module. It is based on the ESP32 microcontroller that boasts Wifi, Bluetooth, Ethernet and Low Power support all in a single chip. (vanepp) made breadboard work, adjusted pin numbering and labels and reduced size of schematic and cleaned up pcb. This chip is 30pins long (2 x15) and 11 pins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
